# Fritzing sketch DimmerAcOrganizado (saved by Fritzing 0.7.10b)

parts:
  R22 = 47k Ω Resistor [package=THT]
  R23 = 47k Ω Resistor [package=THT]
  R24 = 47k Ω Resistor [package=THT]
  R25 = 47k Ω Resistor [package=THT]
  4n35 = Optocoupler [package=THT]
  TRI4 = BTA Triac [package="TO220 [THT]"]
  R26 = 330 Ω Resistor [package=THT]
  R27 = 330 Ω Resistor [package=THT]
  R28 = 330 Ω Resistor [package=THT]
  Rede_AC = Screw terminal - 2 pins [package=THT]
  Lâmpada = Screw terminal - 2 pins [package=THT]
  MOC3021 = Optocoupler [package=THT]
  ATTINY85 = IC, DIP package, 8 pins [chip_label=IC]

nets:
  N1: R22.Pin_0, R23.Pin_0, Rede_AC.pin1, Lâmpada.pin2
  N2: R22.Pin_1, R23.Pin_1, 4n35.Pin_2
  N3: R24.Pin_0, R25.Pin_0, TRI4.A1, R26.Pin_0, Rede_AC.pin2
  N4: R24.Pin_1, R25.Pin_1, 4n35.Pin_1
  N5: 4n35.Pin_4, MOC3021.Pin_2, ATTINY85.pin4
  N6: 4n35.Pin_5, R27.Pin_0, ATTINY85.pin7
  N7: TRI4.A2, Lâmpada.pin1
  N8: TRI4.G, MOC3021.Pin_6
  N9: R26.Pin_1, MOC3021.Pin_4
  N10: R27.Pin_1, ATTINY85.pin8
  N11: R28.Pin_0, MOC3021.Pin_1
  N12: R28.Pin_1, ATTINY85.pin6

custom parts:
  BTA Triac: BTA16
